# Fritzing sketch Наглядная Схема проекта (saved by Fritzing 0.9.4)

parts:
  Компонент1 = Arduino Nano (Rev3.0)
  U1 = 555 Timer [package="DIP8 [THT]"]
  R1 = Resistor [tolerance=±5% resistance=10k package=THT]
  C1 = Film/Foil Capacitor [capacitance=100nF voltage=35V package="10mm [THT, pp]"]
  R3 = Resistor [tolerance=±5% resistance=1.5k package=THT]
  R3_2 = Resistor [tolerance=±0.05% resistance=2.2k package=THT]
  C2 = Electrolytic Capacitor [capacitance=1000μF package="1010 [SMD, electrolytic]"]
  LED1 = 7-SEGMENT-4DIGIT-YOUNGSUN [package=7-segment-4digit-youngsun-longpads]
  R4 = Resistor [tolerance=±5% resistance=220 package=THT]
  R5 = Resistor [tolerance=±5% resistance=220 package=THT]
  R6 = Resistor [tolerance=±5% resistance=220 package=THT]
  R7 = Resistor [tolerance=±5% resistance=220 package=THT]
  R8 = Resistor [tolerance=±5% resistance=220 package=THT]
  R9 = Resistor [tolerance=±5% resistance=220 package=THT]
  R10 = Resistor [tolerance=±5% resistance=220 package=THT]

nets:
  N1: Компонент1.D2, R4.Pin_0
  N2: Компонент1.D3, R5.Pin_0
  N3: Компонент1.D4, R6.Pin_0
  N4: Компонент1.D5, R7.Pin_1
  N5: Компонент1.D6, R8.Pin_1
  N6: Компонент1.D7, R9.Pin_0
  N7: Компонент1.D8, R10.Pin_0
  N8: Компонент1.D11/MOSI, U1.Trigger
  N9: Компонент1.D12/MISO, U1.Output
  N10: Компонент1.A3, LED1.DIG4
  N11: Компонент1.A2, LED1.DIG3
  N12: Компонент1.A1, LED1.DIG2
  N13: Компонент1.A0, LED1.DIG1
  N14: U1.Reset, R1.Pin_1
  N15: U1.Control_Voltage, C1.-
  N16: U1.Threshold, R3_2.Pin_1, C2.+
  N17: U1.Vcc_Supply_Voltage, R1.Pin_0, R3.Pin_1
  N18: C1.+, C2.-
  N19: LED1.D, R7.Pin_0
  N20: LED1.E, R8.Pin_0
  N21: LED1.F, R9.Pin_1
  N22: LED1.COL-C, R6.Pin_1
  N23: LED1.A, R4.Pin_1
  N24: LED1.G, R10.Pin_1
  N25: LED1.B, R5.Pin_1
