# Fritzing sketch Untitled Sketch 3 (saved by Fritzing 0.9.4)

parts:
  Компонент1 = Arduino Nano (Rev3.0)  # not connected
  U1 = 555 Timer [package="DIP8 [THT]"]
  R1 = Resistor [tolerance=±5% resistance=10k package=THT]
  C1 = Film/Foil Capacitor [capacitance=100nF voltage=35V package="10mm [THT, pp]"]
  LED1 = 7-SEGMENT-4DIGIT [package=7-segment-4digit]  # not connected
  R3 = Resistor [tolerance=±5% resistance=1.5k package=THT]
  R3_2 = Resistor [tolerance=±0.05% resistance=2.2k package=THT]
  C2 = Electrolytic Capacitor [capacitance=1000μF package="1010 [SMD, electrolytic]"]

nets:
  N1: U1.Trigger, R3.Pin_0
  N2: U1.Reset, R1.Pin_1
  N3: U1.Control_Voltage, C1.-
  N4: U1.Threshold, R3_2.Pin_1, C2.+
  N5: U1.Vcc_Supply_Voltage, R1.Pin_0, R3.Pin_1
  N6: C1.+, C2.-
